// Logisim project envy three arch.circ as structural Verilog
module registers (
  input  [3:0] read_address_1,
  input  [3:0] read_address_2,
  input  [31:0] data_in,
  input  [3:0] instr_address,
  input  [1:0] instruction,
  output [31:0] data_one,
  output [31:0] data_two
);

  wire [1:0] demultiplexer_1_out0, demultiplexer_1_out1, demultiplexer_1_out2, demultiplexer_1_out3,
       demultiplexer_1_out4, demultiplexer_1_out5, demultiplexer_1_out6, demultiplexer_1_out7,
       demultiplexer_1_out8, demultiplexer_1_out9, demultiplexer_1_out10, demultiplexer_1_out11,
       demultiplexer_1_out12, demultiplexer_1_out13, demultiplexer_1_out14, demultiplexer_1_out15;
  wire [31:0] register_1_data_out, register_2_data_out, register_3_data_out, register_4_data_out,
       register_5_data_out, register_6_data_out, register_7_data_out, register_8_data_out,
       register_9_data_out, register_10_data_out, register_11_data_out, register_12_data_out,
       register_13_data_out, register_14_data_out, register_15_data_out, register_16_data_out;

  register register_1 (.in_1(demultiplexer_1_out0), .data_in(data_in), .data_out(register_1_data_out));
  register register_2 (.in_1(demultiplexer_1_out1), .data_in(data_in), .data_out(register_2_data_out));
  Multiplexer #(.select(4), .width(32), .disabled(0), .enable("false")) multiplexer_1 (
    .in0(register_1_data_out), .in1(register_2_data_out), .in2(register_3_data_out),
    .in3(register_4_data_out), .in4(register_5_data_out), .in5(register_6_data_out),
    .in6(register_7_data_out), .in7(register_8_data_out), .in8(register_9_data_out),
    .in9(register_10_data_out), .in10(register_11_data_out), .in11(register_12_data_out),
    .in12(register_13_data_out), .in13(register_14_data_out), .in14(register_15_data_out),
    .in15(register_16_data_out), .out(data_one), .sel(read_address_1));
  register register_3 (.in_1(demultiplexer_1_out2), .data_in(data_in), .data_out(register_3_data_out));
  register register_4 (.in_1(demultiplexer_1_out3), .data_in(data_in), .data_out(register_4_data_out));
  register register_5 (.in_1(demultiplexer_1_out4), .data_in(data_in), .data_out(register_5_data_out));
  Demultiplexer #(.select(4), .width(2), .disabled(0), .enable("false")) demultiplexer_1 (
    .out0(demultiplexer_1_out0), .out1(demultiplexer_1_out1), .out2(demultiplexer_1_out2),
    .out3(demultiplexer_1_out3), .out4(demultiplexer_1_out4), .out5(demultiplexer_1_out5),
    .out6(demultiplexer_1_out6), .out7(demultiplexer_1_out7), .out8(demultiplexer_1_out8),
    .out9(demultiplexer_1_out9), .out10(demultiplexer_1_out10), .out11(demultiplexer_1_out11),
    .out12(demultiplexer_1_out12), .out13(demultiplexer_1_out13), .out14(demultiplexer_1_out14),
    .out15(demultiplexer_1_out15), .in(instruction), .sel(instr_address));
  register register_6 (.in_1(demultiplexer_1_out5), .data_in(data_in), .data_out(register_6_data_out));
  register register_7 (.in_1(demultiplexer_1_out6), .data_in(data_in), .data_out(register_7_data_out));
  register register_8 (.in_1(demultiplexer_1_out7), .data_in(data_in), .data_out(register_8_data_out));
  register register_9 (.in_1(demultiplexer_1_out8), .data_in(data_in), .data_out(register_9_data_out));
  register register_10 (.in_1(demultiplexer_1_out9), .data_in(data_in), .data_out(register_10_data_out));
  register register_11 (.in_1(demultiplexer_1_out10), .data_in(data_in), .data_out(register_11_data_out));
  register register_12 (.in_1(demultiplexer_1_out11), .data_in(data_in), .data_out(register_12_data_out));
  Multiplexer #(.select(4), .width(32), .disabled(0), .enable("false")) multiplexer_2 (
    .in0(register_1_data_out), .in1(register_2_data_out), .in2(register_3_data_out),
    .in3(register_4_data_out), .in4(register_5_data_out), .in5(register_6_data_out),
    .in6(register_7_data_out), .in7(register_8_data_out), .in8(register_9_data_out),
    .in9(register_10_data_out), .in10(register_11_data_out), .in11(register_12_data_out),
    .in12(register_13_data_out), .in13(register_14_data_out), .in14(register_15_data_out),
    .in15(register_16_data_out), .out(data_two), .sel(read_address_2));
  register register_13 (.in_1(demultiplexer_1_out12), .data_in(data_in), .data_out(register_13_data_out));
  register register_14 (.in_1(demultiplexer_1_out13), .data_in(data_in), .data_out(register_14_data_out));
  register register_15 (.in_1(demultiplexer_1_out14), .data_in(data_in), .data_out(register_15_data_out));
  register register_16 (.in_1(demultiplexer_1_out15), .data_in(data_in), .data_out(register_16_data_out));
endmodule

module register (
  input  [1:0] in_1,
  input  [31:0] data_in,
  output [31:0] data_out
);

  wire and_1_out, clock_1_out, or_1_out;

  and and_1 (and_1_out, in_1[0], in_1[1]);
  or or_1 (or_1_out, and_1_out, in_1[0]);
  Counter #(.width(32), .max('hffffffff)) counter_1 (
    .load(or_1_out), .D(data_in), .count(in_1[1]), .Q(data_out), .clk(clock_1_out));  // open: carry, clr
  Clock clock_1 (.out(clock_1_out));
endmodule

module core (
  input  [31:0] core_in,
  output [31:0] out_2,
  output [7:0] porn_num,
  output [7:0] out_4
);

  wire clock_1_out, clock_2_out, clock_3_out, clock_4_out, clock_5_out, clock_6_out, clock_7_out,
       clu_1_code_in, clu_1_code_mem_in, clu_1_code_mem_out, clu_1_code_out, clu_1_data_in, clu_1_data_out,
       clu_1_ir_in, clu_1_ir_out, clu_1_pc_count, undriven, undriven_3, undriven_4;
  wire [6:0] alu_1_flags;
  wire [7:0] undriven_2;
  wire [15:0] counter_1_q, register_2_q, register_3_q;
  wire [23:0] controlled_buffer_1_out;
  wire [31:0] alu_1_output, controlled_buffer_2_out, controlled_buffer_3_out, ram_1_data, ram_2_data,
       register_1_q, registers_1_data_one, registers_1_data_two;

  Register #(.width(32)) register_1 (
    .D(controlled_buffer_2_out), .en(clu_1_ir_in), .Q(register_1_q), .clk(clock_1_out));  // open: clr
  Clock clock_1 (.out(clock_1_out));
  Register #(.width(16)) register_2 (
    .D({controlled_buffer_1_out[19:16], controlled_buffer_1_out[11:0]}), .en(clu_1_code_mem_in),
    .Q(register_2_q), .clk(clock_2_out));  // open: clr
  Clock clock_2 (.out(clock_2_out));
  assign {controlled_buffer_1_out[23:16], controlled_buffer_1_out[19:16], controlled_buffer_1_out[11:0]} = clu_1_ir_out ? register_1_q[23:0] : 24'bz;  // Controlled_Buffer controlled_buffer_1
  Clock clock_3 (.out(clock_3_out));
  clu clu_1 (
    .opcode(register_1_q[31:24]), .ir_in(clu_1_ir_in), .ir_out(clu_1_ir_out), .data_in(clu_1_data_in),
    .data_out(clu_1_data_out), .code_in(clu_1_code_in), .code_out(clu_1_code_out),
    .code_mem_in(clu_1_code_mem_in), .code_mem_out(clu_1_code_mem_out), .pc_count(clu_1_pc_count));  // open: pc_out, pc_load, pc_load_flag, reg_inst, alu_instr, flag_address, out_17, out_18, out_19, out_20, out_21, out_22, out_23, out_24, out_25, out_26, out_27
  RAM #(.addrWidth(16), .dataWidth(32), .bus("separate")) ram_1 (
    .addr(register_2_q), .data(ram_1_data), .str(clu_1_code_in), .clk(clock_3_out), .ld(clu_1_code_out));  // open: din, sel, clr
  assign controlled_buffer_2_out = clu_1_code_out ? ram_1_data : 32'bz;  // Controlled_Buffer controlled_buffer_2
  Register #(.width(16)) register_3 (
    .D({controlled_buffer_1_out[19:16], controlled_buffer_1_out[11:0]}), .en(clu_1_code_mem_out),
    .Q(register_3_q), .clk(clock_4_out));  // open: clr
  Clock clock_4 (.out(clock_4_out));
  Clock clock_5 (.out(clock_5_out));
  assign controlled_buffer_3_out = undriven ? core_in : 32'bz;  // Controlled_Buffer controlled_buffer_3
  assign porn_num = undriven ? undriven_2 : 8'bz;  // Controlled_Buffer controlled_buffer_4
  RAM #(.addrWidth(16), .dataWidth(32), .bus("separate")) ram_2 (
    .addr(register_3_q), .data(ram_2_data), .str(clu_1_data_in), .clk(clock_5_out), .ld(clu_1_data_out));  // open: din, sel, clr
  Controlled_Buffer #(.width(32)) controlled_buffer_5 (.in(ram_2_data), .en(clu_1_data_out));  // open: out
  assign out_2 = undriven_3 ? controlled_buffer_3_out : 32'bz;  // Controlled_Buffer controlled_buffer_6
  assign out_4 = undriven_3 ? undriven_2 : 8'bz;  // Controlled_Buffer controlled_buffer_7
  Controlled_Buffer #(.width(32)) controlled_buffer_8 (.in(registers_1_data_one));  // open: out, en
  flag_comparitor flag_comparitor_1 ();  // open: address, flags, out_3
  Counter #(.width(16), .max('hffff)) counter_1 (
    .count(clu_1_pc_count), .Q(counter_1_q), .clk(clock_6_out));  // open: load, D, carry, clr
  Controlled_Buffer #(.width(16)) controlled_buffer_9 (.in(counter_1_q));  // open: out, en
  Clock clock_6 (.out(clock_6_out));
  registers registers_1 (
    .read_address_1(controlled_buffer_1_out[19:16]), .read_address_2(controlled_buffer_1_out[19:16]),
    .instr_address(controlled_buffer_1_out[23:20]), .data_one(registers_1_data_one),
    .data_two(registers_1_data_two));  // open: data_in, instruction
  alu alu_1 (.data_B(registers_1_data_two), .\output (alu_1_output), .flags(alu_1_flags));  // open: data_A, mode
  Register #(.width(7)) register_4 (.D(alu_1_flags), .en(undriven_4), .clk(clock_7_out));  // open: Q, clr
  Clock clock_7 (.out(clock_7_out));
  Controlled_Buffer #(.width(32)) controlled_buffer_10 (.in(registers_1_data_two));  // open: out, en
  Controlled_Buffer #(.width(32)) controlled_buffer_11 (.in(alu_1_output), .en(undriven_4));  // open: out
endmodule

module alu (
  input  [31:0] data_A,
  input  [31:0] data_B,
  input  [3:0] mode,
  output [31:0] \output ,
  output [6:0] flags
);

  wire [31:0] adder_1_out, and_1_out, divider_1_out, multiplier_1_out, nand_1_out, nor_1_out, or_1_out,
       shifter_1_out, shifter_2_out, subtractor_1_out, xor_1_out, xor_2_out;

  Comparator #(.width(32), .mode("unsigned")) comparator_1 (
    .a(\output ), .b({32{1'b0}}), .eq(flags[2]));  // open: gt, lt
  Comparator #(.width(32), .mode("unsigned")) comparator_2 (
    .a(data_A), .b(data_B), .gt(flags[3]), .eq(flags[4]), .lt(flags[5]));
  not not_1 (flags[6], flags[4]);
  Adder #(.width(32)) adder_1 (.a(data_A), .b(data_B), .out(adder_1_out), .cout(flags[0]));  // open: cin
  Subtractor #(.width(32)) subtractor_1 (.a(data_A), .b(data_B), .out(subtractor_1_out), .bout(flags[1]));  // open: bin
  Multiplier #(.width(32)) multiplier_1 (.a(data_A), .b(data_B), .out(multiplier_1_out));  // open: cin, cout
  Divider #(.width(32)) divider_1 (.a(data_A), .b(data_B), .out(divider_1_out));  // open: upper, rem
  Multiplexer #(.select(4), .width(32), .disabled(0), .enable("false")) multiplexer_1 (
    .in0(adder_1_out), .in1(subtractor_1_out), .in2(multiplier_1_out), .in3(shifter_2_out),
    .in4(divider_1_out), .in5(shifter_1_out), .in6(and_1_out), .in7(or_1_out), .in8(xor_1_out),
    .in9(nand_1_out), .in10(nor_1_out), .in11(xor_2_out), .out(\output ), .sel(mode));  // open: in12, in13, in14, in15
  Shifter #(.width(32), .shift("lr")) shifter_1 (.in(data_A), .\dist (data_B[4:0]), .out(shifter_1_out));
  Shifter #(.width(32)) shifter_2 (.in(data_A), .\dist (data_B[4:0]), .out(shifter_2_out));
  assign and_1_out = data_A & data_B;  // AND_Gate and_1, 32 bits wide
  assign or_1_out = data_A | data_B;  // OR_Gate or_1, 32 bits wide
  assign xor_1_out = data_A ^ data_B;  // XOR_Gate xor_1, 32 bits wide
  assign nand_1_out = ~(data_A & data_B);  // NAND_Gate nand_1, 32 bits wide
  assign nor_1_out = ~(data_A | data_B);  // NOR_Gate nor_1, 32 bits wide
  assign xor_2_out = data_A ^ data_B;  // XOR_Gate xor_2, 32 bits wide
endmodule

module clu (
  input  [7:0] opcode,
  output ir_in,
  output ir_out,
  output data_in,
  output data_out,
  output code_in,
  output code_out,
  output code_mem_in,
  output code_mem_out,
  output pc_count,
  output pc_out,
  output pc_load,
  output pc_load_flag,
  output [1:0] reg_inst,
  output [3:0] alu_instr,
  output [2:0] flag_address,
  output out_17,
  output out_18,
  output out_19,
  output out_20,
  output out_21,
  output out_22,
  output out_23,
  output out_24,
  output out_25,
  output out_26,
  output out_27
);

  wire [0:0] counter_1_q;

  Counter #(.width(1), .max('h1)) counter_1 (.Q(counter_1_q[0]));  // open: load, D, count, carry, clk, clr
  ROM #(.addrWidth(9), .dataWidth(32)) rom_1 (
    .addr({opcode, counter_1_q[0]}),
    .data({out_27, out_26, out_25, out_24, out_23, out_22, out_21, out_20, out_19, out_18, out_17, flag_address, alu_instr, reg_inst, pc_load_flag, pc_load, pc_out, pc_count, code_mem_out, code_mem_in, code_out, code_in, data_out, data_in, ir_out, ir_in}));  // open: sel
  Pull_Resistor pull_resistor_1 (.node({out_27, out_26, out_25, out_24, out_23, out_22, out_21, out_20, out_19, out_18, out_17, flag_address, alu_instr, reg_inst, pc_load_flag, pc_load, pc_out, pc_count, code_mem_out, code_mem_in, code_out, code_in, data_out, data_in, ir_out, ir_in}));
endmodule

module flag_comparitor (
  input  [2:0] address,
  input  [6:0] flags,
  output out_3
);

  wire controlled_buffer_1_out, controlled_buffer_2_out, controlled_buffer_3_out, controlled_buffer_4_out,
       controlled_buffer_5_out, controlled_buffer_6_out, controlled_buffer_7_out, decoder_1_out1,
       decoder_1_out2, decoder_1_out3, decoder_1_out4, decoder_1_out5, decoder_1_out6, decoder_1_out7,
       or_1_out, or_2_out, or_3_out, or_4_out, or_5_out, or_6_out, or_7_out;

  Decoder #(.select(3), .disabled(0), .enable("false")) decoder_1 (
    .out1(decoder_1_out1), .out2(decoder_1_out2), .out3(decoder_1_out3), .out4(decoder_1_out4),
    .out5(decoder_1_out5), .out6(decoder_1_out6), .out7(decoder_1_out7), .sel(address));  // open: out0
  assign controlled_buffer_1_out = decoder_1_out1 ? flags[0] : 1'bz;  // Controlled_Buffer controlled_buffer_1
  assign controlled_buffer_2_out = decoder_1_out2 ? flags[1] : 1'bz;  // Controlled_Buffer controlled_buffer_2
  assign controlled_buffer_3_out = decoder_1_out3 ? flags[2] : 1'bz;  // Controlled_Buffer controlled_buffer_3
  assign controlled_buffer_4_out = decoder_1_out4 ? flags[3] : 1'bz;  // Controlled_Buffer controlled_buffer_4
  assign controlled_buffer_5_out = decoder_1_out5 ? flags[4] : 1'bz;  // Controlled_Buffer controlled_buffer_5
  assign controlled_buffer_6_out = decoder_1_out6 ? flags[5] : 1'bz;  // Controlled_Buffer controlled_buffer_6
  assign controlled_buffer_7_out = decoder_1_out7 ? flags[6] : 1'bz;  // Controlled_Buffer controlled_buffer_7
  or or_1 (or_1_out, ~decoder_1_out1, controlled_buffer_1_out);  // OR_Gate
  or or_2 (or_2_out, ~decoder_1_out2, controlled_buffer_2_out);  // OR_Gate
  or or_3 (or_3_out, ~decoder_1_out3, controlled_buffer_3_out);  // OR_Gate
  or or_4 (or_4_out, ~decoder_1_out4, controlled_buffer_4_out);  // OR_Gate
  or or_5 (or_5_out, ~decoder_1_out5, controlled_buffer_5_out);  // OR_Gate
  or or_6 (or_6_out, ~decoder_1_out6, controlled_buffer_6_out);  // OR_Gate
  or or_7 (or_7_out, ~decoder_1_out7, controlled_buffer_7_out);  // OR_Gate
  and and_1 (out_3, or_1_out, or_2_out, or_3_out, or_4_out, or_5_out, or_6_out, or_7_out);
endmodule
